# Fritzing sketch opentempescope (saved by Fritzing 0.9.2b)
breadboards: 1

parts:
  U2 = NodeMCU V1.0
  IC1 = ULN2003A [package="SO16 [SMD]"]
  U3 = RELAY [package=relay-g5q]
  LED1 = RGB LED - (4 legs) [package="5 mm [THT]"]
  LED2 = RGB LED - (4 legs) [package="5 mm [THT]"]
  LED3 = RGB LED - (4 legs) [package="5 mm [THT]"]
  R1 = Resistor [tolerance=±5% resistance=100 package=THT]
  R2 = Resistor [tolerance=±5% resistance=50 package=THT]
  R3 = Resistor [tolerance=±5% resistance=50 package=THT]
  R4 = Resistor [tolerance=±5% resistance=100 package=THT]
  R6 = Resistor [tolerance=±5% resistance=50 package=THT]
  R5 = Resistor [tolerance=±5% resistance=50 package=THT]
  R7 = Resistor [tolerance=±5% resistance=100 package=THT]
  R9 = Resistor [tolerance=±5% resistance=50 package=THT]
  R8 = Resistor [tolerance=±5% resistance=50 package=THT]
  U1 = mystery part, 3 pins [chip_label="LM2596 24v -> 5v"]
  JP1 = Header 2 [package=screwterminal-3.5mm-2_lock]
  JP2 = Header 2 [package=screwterminal-3.5mm-2_lock]
  JP3 = Header 2 [package=screwterminal-3.5mm-2_lock]
  S1 = Pushbutton [package="[THT]"]
  R10 = Resistor [tolerance=±5% resistance=10k package=THT]

nets:
  N1: U2.D0, IC1.In_1
  N2: U2.D1, IC1.In_2
  N3: U2.D2, IC1.In_3
  N4: U2.D5, IC1.In_4
  N5: U2.D6, IC1.In_5
  N6: U2.D7, IC1.In_6
  GND: U2.GND, IC1.0V, U1.pin2, JP1.2, R10.Pin_0
  N7: U2.Vin, IC1.COM_-_Common, U3.COIL1, LED1.common_anode, LED2.common_anode, LED3.common_anode, U1.pin3, JP2.1, JP3.1
  N8: U2.3V3, S1.Pin_4
  N9: U2.A0, R10.Pin_1
  N10: IC1.Out_6, R3.Pin_0, R6.Pin_0, R9.Pin_0
  N11: IC1.Out_5, R2.Pin_0, R5.Pin_0, R8.Pin_0
  N12: IC1.Out_4, R1.Pin_0, R4.Pin_0, R7.Pin_0
  N13: IC1.Out_3, JP3.2
  N14: IC1.Out_2, JP2.2
  N15: IC1.Out_1, U3.COIL2
  N16: U3.MAIN, JP1.1
  24V: U3.NO, U1.pin1
  N17: LED1.red_cathode, R1.Pin_1
  N18: LED1.green_cathode, R2.Pin_1
  N19: LED1.blue_cathode, R3.Pin_1
  N20: LED2.red_cathode, R4.Pin_1
  N21: LED2.green_cathode, R5.Pin_1
  N22: LED2.blue_cathode, R6.Pin_1
  N23: LED3.red_cathode, R7.Pin_1
  N24: LED3.green_cathode, R8.Pin_1
  N25: LED3.blue_cathode, R9.Pin_1

custom parts:
  NodeMCU V1.0: ESP8266 based NodeMCU
